// Logisim project TN1.circ as structural Verilog: 1 circuit, main circuit main
module main (
  input  A,
  input  B,
  input  C,
  output NOT_A,
  output AND,
  output OR,
  output NAND,
  output A_NAND_B__NAND_C,
  output NOR,
  output XOR,
  output XNOR,
  output XOR3,
  output NAND3
);

  not not_1 (NOT_A, A);
  and and_1 (AND, A, B);
  or or_1 (OR, A, B);
  nand nand_1 (NAND, A, B);
  nor nor_1 (NOR, A, B);
  xor xor_1 (XOR, A, B);
  xnor xnor_1 (XNOR, A, B);
  xor xor_2 (XOR3, A, B, C);
  nand nand_2 (NAND3, A, B, C);
  nand nand_3 (A_NAND_B__NAND_C, NAND, C);
endmodule
