// Logisim project TN2.circ as structural Verilog: 1 circuit, main circuit main
module main (
  input  x,
  input  y,
  input  z,
  output EQ1,
  output EQ2,
  output EQ3,
  output EQ4,
  output EQ5
);

  wire and_1_out, nor_out, not_1_out, not_2_out, not_3_out, or_1_out, or_2_out, x_prime_y_out,
       x_prime_y_prime_2_out, x_prime_y_prime_out, x_y_2_out, x_y_out, x_z_out, yz_out;

  not not_1 (not_1_out, x);
  not not_2 (not_2_out, y);
  nor \nor  (nor_out, x, y);
  and x_prime_y_prime (x_prime_y_prime_out, not_1_out, not_2_out);
  and x_y (x_y_out, x, y);
  and x_prime_y_prime_2 (x_prime_y_prime_2_out, not_1_out, not_2_out);
  and yz (yz_out, y, z);
  or x_y_2 (x_y_2_out, x, y);
  or x_z (x_z_out, x, z);
  and x_prime_y (x_prime_y_out, not_1_out, y);
  not not_3 (not_3_out, x_y_out);
  or or_1 (or_1_out, x, yz_out);
  and and_1 (and_1_out, x_y_2_out, x_z_out);
  or or_2 (or_2_out, x, x_prime_y_out);
  xnor xnor_1 (EQ1, nor_out, x_prime_y_prime_out);
  xnor xnor_2 (EQ2, not_3_out, x_prime_y_prime_2_out);
  xnor xnor_3 (EQ3, or_1_out, and_1_out);
  xnor xnor_4 (EQ4, or_2_out, x);
  xnor xnor_5 (EQ5, or_2_out, x_y_2_out);
endmodule
